// Logisim project final.circ as structural Verilog: 3 circuits, main circuit main
module main (
);

  wire Clk, multiplexer_6_out, RAMWrNext3, Rst;
  wire [2:0] durum, durumNext0, durumNext1, durumNext2, multiplexer_1_out;
  wire [5:0] MARNext0, MARNext1, MARNext2, MARNext3, multiplexer_2_out, multiplexer_5_out, pcNext1, pcNext2;
  wire [9:0] ACC, ACCNext3, IR, IRNext1, MDRIn, MDRInNext3, multiplexer_3_out, multiplexer_4_out;

  Button Reset (.out(Rst));
  Clock SaatClk (.out(Clk));
  Multiplexer #(.select(3), .width(3), .enable("false")) multiplexer_1 (
    .in0(durumNext0), .in1(durumNext1), .in2(durumNext2), .in3(3'b000), .in4(durum), .in5(3'b000),
    .in6(3'b000), .in7(3'b000), .out(multiplexer_1_out), .sel(durum));
  Multiplexer #(.select(3), .width(6), .enable("false")) multiplexer_2 (
    .in0(MARNext0), .in1(pcNext1), .in2(pcNext2), .in3(MARNext0), .in4(MARNext0), .in5({6{1'b0}}),
    .in6({6{1'b0}}), .in7({6{1'b0}}), .out(multiplexer_2_out), .sel(durum));
  Multiplexer #(.select(3), .width(10), .enable("false")) multiplexer_3 (
    .in0(IR), .in1(IRNext1), .in2(IR), .in3(IR), .in4(IR), .in5({10{1'b0}}), .in6({10{1'b0}}),
    .in7({10{1'b0}}), .out(multiplexer_3_out), .sel(durum));
  Multiplexer #(.select(3), .width(10), .enable("false")) multiplexer_4 (
    .in0(ACC), .in1(ACC), .in2(ACC), .in3(ACCNext3), .in4(ACC), .in5({10{1'b0}}), .in6({10{1'b0}}),
    .in7({10{1'b0}}), .out(multiplexer_4_out), .sel(durum));
  Register #(.width(3)) register_1 (.D(multiplexer_1_out), .en(1'b1), .clk(Clk), .Q(durum), .clr(Rst));
  Register #(.width(6)) register_2 (.D(multiplexer_2_out), .en(1'b1), .clk(Clk), .Q(MARNext0), .clr(Rst));
  Register #(.width(10)) register_3 (.D(multiplexer_3_out), .en(1'b1), .clk(Clk), .Q(IR), .clr(Rst));
  Register #(.width(10)) register_4 (.D(multiplexer_4_out), .en(1'b1), .clk(Clk), .Q(ACC), .clr(Rst));
  Multiplexer #(.select(3), .width(6), .enable("false")) multiplexer_5 (
    .in0(MARNext0), .in1(MARNext1), .in2(MARNext2), .in3(MARNext3), .in4({6{1'b0}}), .in5({6{1'b0}}),
    .in6({6{1'b0}}), .in7({6{1'b0}}), .out(multiplexer_5_out), .sel(durum));
  Multiplexer #(.select(3), .enable("false")) multiplexer_6 (
    .in0(1'b0), .in1(1'b0), .in2(1'b0), .in3(RAMWrNext3), .in4(1'b0), .in5(1'b0), .in6(1'b0), .in7(1'b0),
    .out(multiplexer_6_out), .sel(durum));
  Multiplexer #(.select(3), .width(10), .enable("false")) multiplexer_7 (
    .in0({10{1'b0}}), .in1({10{1'b0}}), .in2({10{1'b0}}), .in3(MDRInNext3), .in4({10{1'b0}}),
    .in5({10{1'b0}}), .in6({10{1'b0}}), .in7({10{1'b0}}), .out(MDRIn), .sel(durum));
  RAM #(.addrWidth(6), .dataWidth(10), .databus("bibus")) RAM10Bit (
    .addr(multiplexer_5_out), .we(multiplexer_6_out), .oe(1'b1), .clk(Clk), .din(MDRIn), .dout(IRNext1));
  Adder #(.width(3)) adder_1 (.a(durum), .b(3'b001), .out(durumNext0));  // open: cin, cout
  Adder #(.width(3)) adder_2 (.a(durum), .b(3'b001), .out(durumNext1));  // open: cin, cout
  Adder #(.width(6)) adder_3 (.a(MARNext0), .b(6'b000001), .out(pcNext1));  // open: cin, cout
  durum2 Durum2 (.PC(MARNext0), .ACC(ACC), .IR(IR), .PCNext2(pcNext2), .MARNext2(MARNext2), .DurumNext2(durumNext2));
  durum3 Durum3 (
    .MDRIn(MDRIn), .ACC(ACC), .MDROut(IRNext1), .IR(IR), .MDRIn_2(MDRInNext3), .MAR(MARNext3),
    .ACC_2(ACCNext3), .RAMWr(RAMWrNext3));

  // Other names for the same wires on the sheet: ACCNext0[9:0] = ACC; ACCNext1[9:0] = ACC; ACCNext2[9:0] = ACC;
  //   ACCNext4[9:0] = ACC; durumNext4[2:0] = durum; IRNext0[9:0] = IR; IRNext2[9:0] = IR; IRNext3[9:0] = IR;
  //   IRNext4[9:0] = IR; MDROut[9:0] = IRNext1; PC[5:0] = MARNext0; pcNext0[5:0] = MARNext0; pcNext3[5:0] = MARNext0;
  //   pcNext4[5:0] = MARNext0

  // Notes on the sheet:
  //   durum
  //   PC
  //   IR
  //   ACC
  //   durumNext
  //   PCNext
  //   IRNext
  //   ACCNext
  //   MAR
  //   RAMWr
  //   MDRIn
  //   durum0
  //   durum1
  //   durum2
  //   durum3
  //   durum4
  //   -----------------------------------------------------------------
  //   -----------------------------------------------------------------
  //   -----------------------------------------------------------------
  //   -----------------------------------------------------------------
  //   -----------------------------------------------------------------
  //   -----------------------------------------------------------------
  //   -----------------------------------------------------------------
  //   -----------------------------------------------------------------
  //   -----------------------------------------------------------------
  //   -----------------------------------------------------------------
  //   -----------------------------------------------------------------
  //   -----------------------------------------------------------------
endmodule

module durum2 (
  input  [5:0] PC,
  input  [9:0] ACC,
  input  [9:0] IR,
  output [5:0] PCNext2,
  output [5:0] MARNext2,
  output [2:0] DurumNext2
);

  wire and_1_out, comparator_1_eq, comparator_2_eq, comparator_2_lt, comparator_3_eq, comparator_4_eq,
       or_1_out;
  wire [2:0] multiplexer_3_out, multiplexer_4_out;

  Comparator #(.width(10)) comparator_1 (.a(ACC), .b({10{1'b0}}), .eq(comparator_1_eq));  // open: gt, lt
  Comparator #(.width(4)) comparator_2 (
    .a(IR[9:6]), .b(4'b0110), .eq(comparator_2_eq), .lt(comparator_2_lt));  // open: gt
  Comparator #(.width(4)) comparator_3 (.a(IR[9:6]), .b(4'b0111), .eq(comparator_3_eq));  // open: gt, lt
  Comparator #(.width(4)) comparator_4 (.a(IR[9:6]), .b(4'b1001), .eq(comparator_4_eq));  // open: gt, lt
  Multiplexer #(.width(6), .enable("false")) multiplexer_1 (.in0(PC), .in1(IR[5:0]), .out(PCNext2), .sel(or_1_out));
  or or_1 (or_1_out, comparator_2_eq, and_1_out);
  and and_1 (and_1_out, comparator_1_eq, comparator_3_eq);
  Multiplexer #(.width(6), .enable("false")) multiplexer_2 (
    .in0({6{1'b0}}), .in1(IR[5:0]), .out(MARNext2), .sel(comparator_2_lt));
  Multiplexer #(.width(3), .enable("false")) multiplexer_3 (
    .in0(3'b000), .in1(3'b011), .out(multiplexer_3_out), .sel(comparator_2_lt));
  Multiplexer #(.width(3), .enable("false")) multiplexer_4 (
    .in0(3'b000), .in1(3'b100), .out(multiplexer_4_out), .sel(comparator_4_eq));
  Adder #(.width(3)) adder_1 (.a(multiplexer_3_out), .b(multiplexer_4_out), .out(DurumNext2));  // open: cin, cout
endmodule

module durum3 (
  input  [9:0] MDRIn,
  input  [9:0] ACC,
  input  [9:0] MDROut,
  input  [9:0] IR,
  output [9:0] MDRIn_2,
  output [5:0] MAR,
  output [9:0] ACC_2,
  output RAMWr
);

  wire comparator_1_eq, comparator_3_eq, comparator_4_eq, comparator_5_eq, comparator_6_eq;
  wire [9:0] adder_1_out, divider_1_out, multiplexer_3_out, multiplexer_4_out, multiplexer_5_out,
       multiplexer_6_out, multiplier_1_out, subtractor_1_out;

  Comparator #(.width(4)) comparator_1 (.a(4'b0000), .b(IR[9:6]), .eq(comparator_1_eq));  // open: gt, lt
  Comparator #(.width(4)) comparator_2 (.a(4'b0001), .b(IR[9:6]), .eq(RAMWr));  // open: gt, lt
  Comparator #(.width(4)) comparator_3 (.a(4'b0010), .b(IR[9:6]), .eq(comparator_3_eq));  // open: gt, lt
  Comparator #(.width(4)) comparator_4 (.a(4'b0011), .b(IR[9:6]), .eq(comparator_4_eq));  // open: gt, lt
  Comparator #(.width(4)) comparator_5 (.a(4'b0100), .b(IR[9:6]), .eq(comparator_5_eq));  // open: gt, lt
  Comparator #(.width(4)) comparator_6 (.a(4'b0101), .b(IR[9:6]), .eq(comparator_6_eq));  // open: gt, lt
  Multiplexer #(.width(6), .enable("false")) multiplexer_1 (.in0({6{1'b0}}), .in1(IR[5:0]), .out(MAR), .sel(RAMWr));
  Multiplexer #(.width(10), .enable("false")) multiplexer_2 (.in0(MDRIn), .in1(ACC), .out(MDRIn_2), .sel(RAMWr));
  Multiplexer #(.width(10), .enable("false")) multiplexer_3 (
    .in0(ACC), .in1(MDROut), .out(multiplexer_3_out), .sel(comparator_1_eq));
  Adder #(.width(10)) adder_1 (.a(multiplexer_3_out), .b(MDROut), .out(adder_1_out));  // open: cin, cout
  Multiplexer #(.width(10), .enable("false")) multiplexer_4 (
    .in0(multiplexer_3_out), .in1(adder_1_out), .out(multiplexer_4_out), .sel(comparator_3_eq));
  Subtractor #(.width(10)) subtractor_1 (.a(multiplexer_4_out), .b(MDROut), .out(subtractor_1_out));  // open: bin, bout
  Multiplexer #(.width(10), .enable("false")) multiplexer_5 (
    .in0(multiplexer_4_out), .in1(subtractor_1_out), .out(multiplexer_5_out), .sel(comparator_4_eq));
  Multiplier #(.width(10)) multiplier_1 (.a(multiplexer_5_out), .b(MDROut), .out(multiplier_1_out));  // open: cin, cout
  Multiplexer #(.width(10), .enable("false")) multiplexer_6 (
    .in0(multiplexer_5_out), .in1(multiplier_1_out), .out(multiplexer_6_out), .sel(comparator_5_eq));
  Divider #(.width(10)) divider_1 (.a(multiplexer_6_out), .b(MDROut), .out(divider_1_out));  // open: upper, rem
  Multiplexer #(.width(10), .enable("false")) multiplexer_7 (
    .in0(multiplexer_6_out), .in1(divider_1_out), .out(ACC_2), .sel(comparator_6_eq));
endmodule
